# Fritzing sketch Untitled Sketch (saved by Fritzing 0.9.3b)
breadboards: 1

parts:
  Componente1 = Arduino Uno (Rev3)
  LDR_tl = Photocell (LDR) [part_number="Top Left (tl)" package=THT]
  LDR_tr = Photocell (LDR) [part_number="Top Right (tr)" package=THT]
  LDR_bt = Photocell (LDR) [part_number="Bottom Left (bt)" package=THT]
  LDR_br = Photocell (LDR) [part_number="Bottom Right (br)" package=THT]
  Componente2 = Bluetooth HC-05 Macho
  S1 = Momentary Switch [package=ksa_sealed_tac_switch]
  LED1 = LED - 5mm [color="Green (560nm)" package="5 mm [THT]"]
  R5 = Resistor [tolerance=±5% resistance=220 package=THT]
  R6 = Resistor [tolerance=±5% resistance=10k package=THT]
  R_tl = Resistor [tolerance=±5% resistance=10k package=THT]
  R_bt = Resistor [tolerance=±5% resistance=10k package=THT]
  R_br = Resistor [tolerance=±5% resistance=10k package=THT]
  R_tr = Resistor [tolerance=±5% resistance=10k package=THT]
  servox = Basic Servo
  servoy = Basic Servo
  R11 = Resistor [tolerance=±5% resistance=1k package=THT]
  R12 = Resistor [tolerance=±5% resistance=2.0k part_number="Divisor de tensio" package=THT]

nets:
  N1: Componente1.A0, LDR_tl.pin_0, R_tl.Pin_0
  N2: Componente1.A1, LDR_tr.pin_1, R_tr.Pin_1
  N3: Componente1.A2, LDR_bt.pin_0, R_bt.Pin_0
  N4: Componente1.A3, LDR_br.pin_1, R_br.Pin_1
  N5: Componente1.D9_PWM, servox.pulse
  N6: Componente1.D10_PWM/SS, servoy.pulse
  N7: Componente1.D2, S1.4, R6.Pin_0
  N8: Componente1.D4, LED1.cathode
  N9: Componente1.D6_PWM, R11.Pin_1
  N10: Componente1.D7, Componente2.TXD
  VCC: Componente1.5V, LDR_tl.pin_1, LDR_tr.pin_0, LDR_bt.pin_1, LDR_br.pin_0, Componente2.VCC, S1.2, servox.vcc, servoy.vcc
  GND: Componente1.GND, Componente2.GND, R5.Pin_1, R6.Pin_1, R_tl.Pin_1, R_bt.Pin_1, R_br.Pin_0, R_tr.Pin_0, servox.gnd, servoy.gnd, R12.Pin_0
  N11: Componente2.RXD, R11.Pin_0, R12.Pin_1
  N12: LED1.anode, R5.Pin_0
